# Fritzing sketch Simple Pulse Monitor (saved by Fritzing 0.9.3b)
circuit board: 8.46667cm x 5.64444cm
breadboards: 1

parts:
  LED1 = LED - 5mm [color="Red (633nm)" package="5 mm [THT]"]
  SEN2 = Pulse Sensor [package=SIP]
  U2 = NodeMCU V1.0

nets:
  GND: LED1.cathode, SEN2.GND, U2.GND
  N1: LED1.anode, U2.D0
  VCC: SEN2.Vcc, U2.Vin
  N2: SEN2.Signal, U2.A0

custom parts:
  Pulse Sensor: Pulse Sensor Optical Heart Rate Monitor for Arduino and other microcontrollers
  NodeMCU V1.0: ESP8266 based NodeMCU

// code stored in the sketch: Simple Pulse Monitor.ino
#include <ThingSpeak.h>


//Watch the YouTubeVideo for Implementation
// https://youtu.be/9F_GURMziec

// Interfacing the Pulse sensior
#include <ESP8266WiFi.h>;
#include <WiFiClient.h>;
#include <ThingSpeak.h>;

const char* ssid = "GEARBOX STAFF"; //Your Network SSID
const char* password = "Staff@Gearbox"; //Your Network Password
int val;
int ledPin= 0;
int PulseSensorpin = A0; //Pulse Sensor Pin Connected at A0 Pin
WiFiClient client;

unsigned long myChannelNumber = 1336230 ; //Your Channel Number (Without Brackets)
const char * myWriteAPIKey = "KA0SECG1AL3WOLH3"; //Your Write API Key

void setup()
{
 Serial.begin(9600);
 delay(10);
  // Connect to WiFi network
  WiFi.begin(ssid, password);
  ThingSpeak.begin(client);
}

void loop()
{
  val = analogRead(PulseSensorpin); //Read Analog values and Store in val variable
  Serial.println("Pulse Sensorvalue=  "); // Start Printing on Pulse sensor value on LCD
  Serial.println(val); // Start Printing on Pulse sensor value on LCD
  delay(10);
  digitalWrite (ledPin, HIGH);
  ThingSpeak.writeField(myChannelNumber, 1,val, myWriteAPIKey); //Update in ThingSpeak
}
